# Fritzing sketch IPWiringDiagram (saved by Fritzing 1.0.2b)

parts:
  Teensy1 = Teensy 4.1
  A1 = Hanmatek HM305
  Yumo-enc1 = YumoE6B2
  Yumo-enc2 = YumoE6B2
  A2 = terminal block 8position
  M1 = DC Motor [voltage_(max)=6V voltage_(min)=3V]
  A3 = MD30C
  part = SO-24x [chip_label=SO-24x package=SO(x)]  # not connected

nets:
  GND: Teensy1.GND, Teensy1.GND2, A2.Pin_4, A2.Pin_13, A3.pin_2, A3.pin_3
  N1: Teensy1.D2, Yumo-enc2.A
  N2: Teensy1.D3, Yumo-enc2.B
  N3: Teensy1.D4, Yumo-enc1.A
  N4: Teensy1.D5, Yumo-enc1.B
  N5: Teensy1.D9, A3.pin_5
  N6: Teensy1.D10, A3.pin_4
  N7: A1.Pin_3, A2.Pin_3, A2.Pin_14
  N8: A1.Pin_4, A2.Pin_1, A2.Pin_16
  N9: Yumo-enc1.V, A2.Pin_6, A2.Pin_11
  N10: Yumo-enc1.GND, A2.Pin_8, A2.Pin_9
  N11: Yumo-enc2.V, A2.Pin_5, A2.Pin_12
  N12: Yumo-enc2.GND, A2.Pin_7, A2.Pin_10
  N13: A2.Pin_2, A2.Pin_15, A3.pin_1
  N14: M1.pin_1, A3.pin_20
  N15: M1.pin_2, A3.pin_19

notes:
  Micro usb to USB
  to computer
  24V
  10A
  ENC1
  ENC2

custom parts:
  Teensy 4.1: The Teensy is a complete USB-based microcontoller development system, in a very small footprint, capable of implementing many types of projects. All programming is done via the USB port. No special programmer is needed, only a standard micro-USB cable and a PC or Macintosh with a USB port.
  Hanmatek HM305: DC Power Supply 30V5A HM305.
